# Fritzing sketch ButonlaLedYakma (saved by Fritzing 0.9.10b)
breadboards: 1

parts:
  Parça1 = Arduino Uno (Rev3)
  LED1 = LED - 5mm [color="Red (633nm)" current=0.030 package="5 mm [THT]"]
  R1 = Resistor [tolerance=±5% power=0.25 resistance=330 package=THT]
  S1 = Pushbutton [package="[THT]"]
  R2 = Resistor [tolerance=±5% power=0.25 resistance=10k package=THT]

nets:
  N1: Parça1.D8, S1.Pin_1, S1.Pin_2, R2.Pin_0
  N2: Parça1.D10_PWM/SS, R1.Pin_0
  N3: Parça1.5V, S1.Pin_3, S1.Pin_4
  N4: Parça1.GND, LED1.cathode, R2.Pin_1
  N5: LED1.anode, R1.Pin_1
