# Fritzing sketch LDR (saved by Fritzing 0.9.10b)
breadboards: 1

parts:
  Parça1 = Arduino Uno (Rev3)
  R1 = Photocell (LDR) [package=THT]
  R2 = Resistor [tolerance=±5% power=0.25 resistance=10k package=THT]
  LED1 = LED - 5mm [color="Red (633nm)" current=0.030 package="5 mm [THT]"]
  R3 = Resistor [tolerance=±5% power=0.25 resistance=330 package=THT]

nets:
  N1: Parça1.A0, R1.pin_1, R2.Pin_0
  N2: Parça1.D3_PWM, R3.Pin_0
  N3: Parça1.5V, R1.pin_0
  N4: Parça1.GND, R2.Pin_1, LED1.cathode
  N5: LED1.anode, R3.Pin_1
