# Fritzing sketch GazSensör (saved by Fritzing 0.9.10b)
breadboards: 1

parts:
  U1 = GAS_SENSOR [package=mq-3]
  Parça1 = Arduino Uno (Rev3)
  J1 = Piezo Speaker
  R1 = Resistor [tolerance=±5% power=0.25 resistance=330 package=THT]

nets:
  N1: U1.B1, Parça1.5V
  N2: U1.A1, Parça1.GND, J1.pin1
  N3: Parça1.D9_PWM, R1.Pin_0
  N4: J1.pin2, R1.Pin_1
