# Fritzing sketch UzaklıkSensörü (saved by Fritzing 0.9.10b)
breadboards: 1

parts:
  Parça1 = Arduino Uno (Rev3)
  HC-SR04_Sensor_1 = HC-SR04 Ultrasonic Distance Sensor
  J1 = Piezo Speaker
  R1 = Resistor [tolerance=±5% power=0.25 resistance=330 package=THT]

nets:
  N1: Parça1.D8, R1.Pin_0
  N2: Parça1.D6_PWM, HC-SR04_Sensor_1.ECHO
  N3: Parça1.D7, HC-SR04_Sensor_1.TRIG
  5V: Parça1.5V, HC-SR04_Sensor_1.VCC
  GND: Parça1.GND, HC-SR04_Sensor_1.GND, J1.pin1
  N4: J1.pin2, R1.Pin_1
