# Fritzing sketch LCDuygulaması (saved by Fritzing 0.9.10b)
breadboards: 1

parts:
  Parça1 = Arduino Uno (Rev3)
  LCD1 = LCD screen
  U1 = POT [knob_status=50% power=0.5W package=pot_mammoth]
  HC-SR04_Sensor_1 = HC-SR04 Ultrasonic Distance Sensor

nets:
  N1: Parça1.D11_PWM/MOSI, LCD1.E
  N2: Parça1.D12/MISO, LCD1.RS
  N3: Parça1.D2, LCD1.DB7
  N4: Parça1.D3_PWM, LCD1.DB6
  N5: Parça1.D4, LCD1.DB5
  N6: Parça1.D5_PWM, LCD1.DB4
  N7: Parça1.D6_PWM, HC-SR04_Sensor_1.ECHO
  N8: Parça1.D7, HC-SR04_Sensor_1.TRIG
  5V: Parça1.5V, LCD1.VDD, LCD1.LED+, U1.S, HC-SR04_Sensor_1.VCC
  GND: Parça1.GND, LCD1.VSS, LCD1.R/W, LCD1.LED-, U1.E, HC-SR04_Sensor_1.GND
  N9: LCD1.V0, U1.A
