# Fritzing sketch dht11 (saved by Fritzing 0.9.10b)
breadboards: 1

parts:
  Parça1 = Arduino Uno (Rev3)
  RHT1 = Humidity and Temperature Sensor RHT03

nets:
  N1: Parça1.D4, RHT1.Vcc
  N2: Parça1.5V, RHT1.Data-signal
  N3: Parça1.GND, RHT1.GND_2
