# Fritzing sketch ds1307uygulama (saved by Fritzing 0.9.10b)
breadboards: 1

parts:
  Parça1 = Arduino Uno (Rev3)
  Parça2 = Real Time Clock Module - DS1307 RTC Breakout Board

nets:
  N1: Parça1.A4/SDA, Parça2.SDA
  N2: Parça1.A5/SCL, Parça2.SCL
  3V3: Parça1.3V3, Parça2.5V
  GND: Parça1.GND, Parça2.GND
