# Fritzing sketch rfid (saved by Fritzing 0.9.10b)
breadboards: 1

parts:
  Parça1 = Arduino Uno (Rev3)
  LED1 = LED - 5mm [color="Red (633nm)" current=0.030 package="5 mm [THT]"]
  LED2 = LED - 5mm [color="Red (633nm)" current=0.030 package="5 mm [THT]"]
  R1 = Resistor [tolerance=±5% power=0.25 resistance=330 package=THT]
  R2 = Resistor [tolerance=±5% power=0.25W resistance=330 package=THT]
  Parça2 = RFID USB Reader

nets:
  N1: Parça1.D9_PWM, Parça2.GND
  N2: Parça1.D10_PWM/SS, Parça2.GNDT
  N3: Parça1.D11_PWM/MOSI, Parça2.ANT2
  N4: Parça1.D12/MISO, Parça2.ANT1
  N5: Parça1.D13/SCK, Parça2.CP
  N6: Parça1.D2, R1.Pin_0
  N7: Parça1.D3_PWM, R2.Pin_1
  3V3: Parça1.3V3, Parça2.VCC
  N8: Parça1.GND, LED1.cathode, LED2.cathode, Parça2.TX-O
  N9: LED1.anode, R1.Pin_1
  N10: LED2.anode, R2.Pin_0

notes:
  RFID-RC522
